# Fritzing sketch circuit-diagram (saved by Fritzing 0.9.6b)

parts:
  U1 = NodeMCU V3.0
  S1 = Pushbutton [package="[THT]"]
  Power_plug1 = Power plug
  S2 = H-Bridge with L298N  # not connected
  A1 = A4988
  M1 = Stepper Motor - Bipolar
  C1 = Electrolytic Capacitor [capacitance=100μF voltage=35V package="0807 [SMD, electrolytic]"]

nets:
  3V3: U1.3V3, A1.VDD
  N1: U1.GND, A1.GND#13
  N2: S1.Pin_3, S1.Pin_4, Power_plug1.VCC, A1.VMOT, C1.+
  N3: Power_plug1.GND, A1.GND#19
  N4: A1.1B, M1.D
  N5: A1.1A, M1.B
  N6: A1.2A, M1.C
  N7: A1.2B, M1.A

custom parts:
  NodeMCU V3.0: ESP8266 based NodeMCU
  H-Bridge with L298N: h-bridge
